// Logisim project ALU.circ as structural Verilog: 15 circuits, main circuit main
module main (
  input  [2:0] Control,
  input  [33:0] A,
  input  [33:0] B,
  output [33:0] Result,
  output Zero,
  output Negative,
  output Overflow,
  output Carry
);

  L_34_bit_ALU l_34_bit_alu_1 (
    .A(A), .B(B), .Control0(Control[0]), .Control1(Control[1]), .control2(Control[2]), .Result(Result),
    .Zero(Zero), .Negative(Negative), .Overflow(Overflow), .Carry(Carry));
endmodule

// 34-bit AND
module L_34_bit_and (
  input  [33:0] A,
  input  [33:0] B,
  output [33:0] Result
);

  assign Result = A & B;  // AND_Gate and_1, 34 bits wide
endmodule

// 34-bit OR
module L_34_bit_OR (
  input  [33:0] A,
  input  [33:0] B,
  output [33:0] Result
);

  assign Result = A | B;  // OR_Gate or_1, 34 bits wide
endmodule

module Full_adder (
  input  Carry_in,
  input  A,
  input  B,
  output Result,
  output Carry_out
);

  wire and_1_out, and_2_out, xor_1_out;

  and and_1 (and_1_out, B, A);
  xor xor_1 (xor_1_out, A, B);
  or or_1 (Carry_out, and_1_out, and_2_out);
  and and_2 (and_2_out, xor_1_out, Carry_in);
  xor xor_2 (Result, Carry_in, xor_1_out);
endmodule

module L_34_bit_full_adder (
  input  Carry_in,
  input  A0,
  input  B0,
  input  A1,
  input  B1,
  input  A2,
  input  B2,
  input  A3,
  input  B3,
  input  A4,
  input  B4,
  input  A5,
  input  B5,
  input  A6,
  input  B6,
  input  A7,
  input  B7,
  input  A8,
  input  B8,
  input  A9,
  input  B9,
  input  A10,
  input  B10,
  input  A11,
  input  B11,
  input  A12,
  input  B12,
  input  A13,
  input  B13,
  input  A14,
  input  B14,
  input  A15,
  input  B15,
  input  A16,
  input  B16,
  input  A17,
  input  B17,
  input  A18,
  input  B18,
  input  A19,
  input  B19,
  input  A20,
  input  B20,
  input  A21,
  input  B21,
  input  A22,
  input  B22,
  input  A23,
  input  B23,
  input  A24,
  input  B24,
  input  A25,
  input  B25,
  input  A26,
  input  B26,
  input  A27,
  input  B27,
  input  A28,
  input  B28,
  input  A29,
  input  B29,
  input  A30,
  input  B30,
  input  A31,
  input  B31,
  input  A32,
  input  B32,
  input  A33,
  input  B33,
  output Result0,
  output Result1,
  output Result2,
  output Result3,
  output Result4,
  output Result5,
  output Result6,
  output Result7,
  output Result8,
  output Result9,
  output Result10,
  output Result11,
  output Result12,
  output Result13,
  output Result14,
  output Result15,
  output Result16,
  output Result17,
  output Result18,
  output Result19,
  output Result20,
  output Result21,
  output Result22,
  output Result23,
  output Result24,
  output Result25,
  output Result26,
  output Result27,
  output Result28,
  output Result29,
  output Result30,
  output Result31,
  output Result32,
  output Result33,
  output Carry
);

  wire full_adder_1_carry_out, full_adder_2_carry_out, full_adder_3_carry_out, full_adder_4_carry_out,
       full_adder_5_carry_out, full_adder_6_carry_out, full_adder_7_carry_out, full_adder_8_carry_out,
       full_adder_9_carry_out, full_adder_10_carry_out, full_adder_11_carry_out, full_adder_12_carry_out,
       full_adder_13_carry_out, full_adder_14_carry_out, full_adder_15_carry_out, full_adder_16_carry_out,
       full_adder_17_carry_out, full_adder_18_carry_out, full_adder_19_carry_out, full_adder_20_carry_out,
       full_adder_21_carry_out, full_adder_22_carry_out, full_adder_23_carry_out, full_adder_24_carry_out,
       full_adder_25_carry_out, full_adder_26_carry_out, full_adder_27_carry_out, full_adder_28_carry_out,
       full_adder_29_carry_out, full_adder_30_carry_out, full_adder_31_carry_out, full_adder_32_carry_out,
       full_adder_33_carry_out;

  Full_adder full_adder_1 (.A(A0), .B(B0), .Carry_in(Carry_in), .Carry_out(full_adder_1_carry_out), .Result(Result0));
  Full_adder full_adder_2 (
    .A(A1), .B(B1), .Carry_in(full_adder_1_carry_out), .Carry_out(full_adder_2_carry_out), .Result(Result1));
  Full_adder full_adder_3 (
    .A(A2), .B(B2), .Carry_in(full_adder_2_carry_out), .Carry_out(full_adder_3_carry_out), .Result(Result2));
  Full_adder full_adder_4 (
    .A(A3), .B(B3), .Carry_in(full_adder_3_carry_out), .Carry_out(full_adder_4_carry_out), .Result(Result3));
  Full_adder full_adder_5 (
    .A(A4), .B(B4), .Carry_in(full_adder_4_carry_out), .Carry_out(full_adder_5_carry_out), .Result(Result4));
  Full_adder full_adder_6 (
    .A(A5), .B(B5), .Carry_in(full_adder_5_carry_out), .Carry_out(full_adder_6_carry_out), .Result(Result5));
  Full_adder full_adder_7 (
    .A(A6), .B(B6), .Carry_in(full_adder_6_carry_out), .Carry_out(full_adder_7_carry_out), .Result(Result6));
  Full_adder full_adder_8 (
    .A(A7), .B(B7), .Carry_in(full_adder_7_carry_out), .Carry_out(full_adder_8_carry_out), .Result(Result7));
  Full_adder full_adder_9 (
    .A(A8), .B(B8), .Carry_in(full_adder_8_carry_out), .Carry_out(full_adder_9_carry_out), .Result(Result8));
  Full_adder full_adder_10 (
    .A(A9), .B(B9), .Carry_in(full_adder_9_carry_out), .Carry_out(full_adder_10_carry_out), .Result(Result9));
  Full_adder full_adder_11 (
    .A(A10), .B(B10), .Carry_in(full_adder_10_carry_out), .Carry_out(full_adder_11_carry_out),
    .Result(Result10));
  Full_adder full_adder_12 (
    .A(A11), .B(B11), .Carry_in(full_adder_11_carry_out), .Carry_out(full_adder_12_carry_out),
    .Result(Result11));
  Full_adder full_adder_13 (
    .A(A12), .B(B12), .Carry_in(full_adder_12_carry_out), .Carry_out(full_adder_13_carry_out),
    .Result(Result12));
  Full_adder full_adder_14 (
    .A(A13), .B(B13), .Carry_in(full_adder_13_carry_out), .Carry_out(full_adder_14_carry_out),
    .Result(Result13));
  Full_adder full_adder_15 (
    .A(A14), .B(B14), .Carry_in(full_adder_14_carry_out), .Carry_out(full_adder_15_carry_out),
    .Result(Result14));
  Full_adder full_adder_16 (
    .A(A15), .B(B15), .Carry_in(full_adder_15_carry_out), .Carry_out(full_adder_16_carry_out),
    .Result(Result15));
  Full_adder full_adder_17 (
    .A(A16), .B(B16), .Carry_in(full_adder_16_carry_out), .Carry_out(full_adder_17_carry_out),
    .Result(Result16));
  Full_adder full_adder_18 (
    .A(A17), .B(B17), .Carry_in(full_adder_17_carry_out), .Carry_out(full_adder_18_carry_out),
    .Result(Result17));
  Full_adder full_adder_19 (
    .A(A18), .B(B18), .Carry_in(full_adder_18_carry_out), .Carry_out(full_adder_19_carry_out),
    .Result(Result18));
  Full_adder full_adder_20 (
    .A(A19), .B(B19), .Carry_in(full_adder_19_carry_out), .Carry_out(full_adder_20_carry_out),
    .Result(Result19));
  Full_adder full_adder_21 (
    .A(A20), .B(B20), .Carry_in(full_adder_20_carry_out), .Carry_out(full_adder_21_carry_out),
    .Result(Result20));
  Full_adder full_adder_22 (
    .A(A21), .B(B21), .Carry_in(full_adder_21_carry_out), .Carry_out(full_adder_22_carry_out),
    .Result(Result21));
  Full_adder full_adder_23 (
    .A(A22), .B(B22), .Carry_in(full_adder_22_carry_out), .Carry_out(full_adder_23_carry_out),
    .Result(Result22));
  Full_adder full_adder_24 (
    .A(A23), .B(B23), .Carry_in(full_adder_23_carry_out), .Carry_out(full_adder_24_carry_out),
    .Result(Result23));
  Full_adder full_adder_25 (
    .A(A24), .B(B24), .Carry_in(full_adder_24_carry_out), .Carry_out(full_adder_25_carry_out),
    .Result(Result24));
  Full_adder full_adder_26 (
    .A(A25), .B(B25), .Carry_in(full_adder_25_carry_out), .Carry_out(full_adder_26_carry_out),
    .Result(Result25));
  Full_adder full_adder_27 (
    .A(A26), .B(B26), .Carry_in(full_adder_26_carry_out), .Carry_out(full_adder_27_carry_out),
    .Result(Result26));
  Full_adder full_adder_28 (
    .A(A27), .B(B27), .Carry_in(full_adder_27_carry_out), .Carry_out(full_adder_28_carry_out),
    .Result(Result27));
  Full_adder full_adder_29 (
    .A(A28), .B(B28), .Carry_in(full_adder_28_carry_out), .Carry_out(full_adder_29_carry_out),
    .Result(Result28));
  Full_adder full_adder_30 (
    .A(A29), .B(B29), .Carry_in(full_adder_29_carry_out), .Carry_out(full_adder_30_carry_out),
    .Result(Result29));
  Full_adder full_adder_31 (
    .A(A30), .B(B30), .Carry_in(full_adder_30_carry_out), .Carry_out(full_adder_31_carry_out),
    .Result(Result30));
  Full_adder full_adder_32 (
    .A(A31), .B(B31), .Carry_in(full_adder_31_carry_out), .Carry_out(full_adder_32_carry_out),
    .Result(Result31));
  Full_adder full_adder_33 (
    .A(A32), .B(B32), .Carry_in(full_adder_32_carry_out), .Carry_out(full_adder_33_carry_out),
    .Result(Result32));
  Full_adder full_adder_34 (.A(A33), .B(B33), .Carry_in(full_adder_33_carry_out), .Carry_out(Carry), .Result(Result33));
endmodule

// FA
module L_34_bit_full_adder_concise (
  input  Carry_in_83e99e4a,
  input  [33:0] A,
  input  [33:0] B,
  output [33:0] Result,
  output Carry
);

  wire full_adder_1_carry_out, full_adder_2_carry_out, full_adder_3_carry_out, full_adder_4_carry_out,
       full_adder_5_carry_out, full_adder_6_carry_out, full_adder_7_carry_out, full_adder_8_carry_out,
       full_adder_9_carry_out, full_adder_10_carry_out, full_adder_11_carry_out, full_adder_12_carry_out,
       full_adder_13_carry_out, full_adder_14_carry_out, full_adder_15_carry_out, full_adder_16_carry_out,
       full_adder_17_carry_out, full_adder_18_carry_out, full_adder_19_carry_out, full_adder_20_carry_out,
       full_adder_21_carry_out, full_adder_22_carry_out, full_adder_23_carry_out, full_adder_24_carry_out,
       full_adder_25_carry_out, full_adder_26_carry_out, full_adder_27_carry_out, full_adder_28_carry_out,
       full_adder_29_carry_out, full_adder_30_carry_out, full_adder_31_carry_out, full_adder_32_carry_out,
       full_adder_33_carry_out;

  Full_adder full_adder_1 (
    .A(A[0]), .B(B[0]), .Carry_in(Carry_in_83e99e4a), .Carry_out(full_adder_1_carry_out), .Result(Result[0]));
  Full_adder full_adder_2 (
    .A(A[1]), .B(B[1]), .Carry_in(full_adder_1_carry_out), .Carry_out(full_adder_2_carry_out),
    .Result(Result[1]));
  Full_adder full_adder_3 (
    .A(A[2]), .B(B[2]), .Carry_in(full_adder_2_carry_out), .Carry_out(full_adder_3_carry_out),
    .Result(Result[2]));
  Full_adder full_adder_4 (
    .A(A[3]), .B(B[3]), .Carry_in(full_adder_3_carry_out), .Carry_out(full_adder_4_carry_out),
    .Result(Result[3]));
  Full_adder full_adder_5 (
    .A(A[4]), .B(B[4]), .Carry_in(full_adder_4_carry_out), .Carry_out(full_adder_5_carry_out),
    .Result(Result[4]));
  Full_adder full_adder_6 (
    .A(A[5]), .B(B[5]), .Carry_in(full_adder_5_carry_out), .Carry_out(full_adder_6_carry_out),
    .Result(Result[5]));
  Full_adder full_adder_7 (
    .A(A[6]), .B(B[6]), .Carry_in(full_adder_6_carry_out), .Carry_out(full_adder_7_carry_out),
    .Result(Result[6]));
  Full_adder full_adder_8 (
    .A(A[7]), .B(B[7]), .Carry_in(full_adder_7_carry_out), .Carry_out(full_adder_8_carry_out),
    .Result(Result[7]));
  Full_adder full_adder_9 (
    .A(A[8]), .B(B[8]), .Carry_in(full_adder_8_carry_out), .Carry_out(full_adder_9_carry_out),
    .Result(Result[8]));
  Full_adder full_adder_10 (
    .A(A[9]), .B(B[9]), .Carry_in(full_adder_9_carry_out), .Carry_out(full_adder_10_carry_out),
    .Result(Result[9]));
  Full_adder full_adder_11 (
    .A(A[10]), .B(B[10]), .Carry_in(full_adder_10_carry_out), .Carry_out(full_adder_11_carry_out),
    .Result(Result[10]));
  Full_adder full_adder_12 (
    .A(A[11]), .B(B[11]), .Carry_in(full_adder_11_carry_out), .Carry_out(full_adder_12_carry_out),
    .Result(Result[11]));
  Full_adder full_adder_13 (
    .A(A[12]), .B(B[12]), .Carry_in(full_adder_12_carry_out), .Carry_out(full_adder_13_carry_out),
    .Result(Result[12]));
  Full_adder full_adder_14 (
    .A(A[13]), .B(B[13]), .Carry_in(full_adder_13_carry_out), .Carry_out(full_adder_14_carry_out),
    .Result(Result[13]));
  Full_adder full_adder_15 (
    .A(A[14]), .B(B[14]), .Carry_in(full_adder_14_carry_out), .Carry_out(full_adder_15_carry_out),
    .Result(Result[14]));
  Full_adder full_adder_16 (
    .A(A[15]), .B(B[15]), .Carry_in(full_adder_15_carry_out), .Carry_out(full_adder_16_carry_out),
    .Result(Result[15]));
  Full_adder full_adder_17 (
    .A(A[16]), .B(B[16]), .Carry_in(full_adder_16_carry_out), .Carry_out(full_adder_17_carry_out),
    .Result(Result[16]));
  Full_adder full_adder_18 (
    .A(A[17]), .B(B[17]), .Carry_in(full_adder_17_carry_out), .Carry_out(full_adder_18_carry_out),
    .Result(Result[17]));
  Full_adder full_adder_19 (
    .A(A[18]), .B(B[18]), .Carry_in(full_adder_18_carry_out), .Carry_out(full_adder_19_carry_out),
    .Result(Result[18]));
  Full_adder full_adder_20 (
    .A(A[19]), .B(B[19]), .Carry_in(full_adder_19_carry_out), .Carry_out(full_adder_20_carry_out),
    .Result(Result[19]));
  Full_adder full_adder_21 (
    .A(A[20]), .B(B[20]), .Carry_in(full_adder_20_carry_out), .Carry_out(full_adder_21_carry_out),
    .Result(Result[20]));
  Full_adder full_adder_22 (
    .A(A[21]), .B(B[21]), .Carry_in(full_adder_21_carry_out), .Carry_out(full_adder_22_carry_out),
    .Result(Result[21]));
  Full_adder full_adder_23 (
    .A(A[22]), .B(B[22]), .Carry_in(full_adder_22_carry_out), .Carry_out(full_adder_23_carry_out),
    .Result(Result[22]));
  Full_adder full_adder_24 (
    .A(A[23]), .B(B[23]), .Carry_in(full_adder_23_carry_out), .Carry_out(full_adder_24_carry_out),
    .Result(Result[23]));
  Full_adder full_adder_25 (
    .A(A[24]), .B(B[24]), .Carry_in(full_adder_24_carry_out), .Carry_out(full_adder_25_carry_out),
    .Result(Result[24]));
  Full_adder full_adder_26 (
    .A(A[25]), .B(B[25]), .Carry_in(full_adder_25_carry_out), .Carry_out(full_adder_26_carry_out),
    .Result(Result[25]));
  Full_adder full_adder_27 (
    .A(A[26]), .B(B[26]), .Carry_in(full_adder_26_carry_out), .Carry_out(full_adder_27_carry_out),
    .Result(Result[26]));
  Full_adder full_adder_28 (
    .A(A[27]), .B(B[27]), .Carry_in(full_adder_27_carry_out), .Carry_out(full_adder_28_carry_out),
    .Result(Result[27]));
  Full_adder full_adder_29 (
    .A(A[28]), .B(B[28]), .Carry_in(full_adder_28_carry_out), .Carry_out(full_adder_29_carry_out),
    .Result(Result[28]));
  Full_adder full_adder_30 (
    .A(A[29]), .B(B[29]), .Carry_in(full_adder_29_carry_out), .Carry_out(full_adder_30_carry_out),
    .Result(Result[29]));
  Full_adder full_adder_31 (
    .A(A[30]), .B(B[30]), .Carry_in(full_adder_30_carry_out), .Carry_out(full_adder_31_carry_out),
    .Result(Result[30]));
  Full_adder full_adder_32 (
    .A(A[31]), .B(B[31]), .Carry_in(full_adder_31_carry_out), .Carry_out(full_adder_32_carry_out),
    .Result(Result[31]));
  Full_adder full_adder_33 (
    .A(A[32]), .B(B[32]), .Carry_in(full_adder_32_carry_out), .Carry_out(full_adder_33_carry_out),
    .Result(Result[32]));
  Full_adder full_adder_34 (
    .A(A[33]), .B(B[33]), .Carry_in(full_adder_33_carry_out), .Carry_out(Carry), .Result(Result[33]));
endmodule

module L_34_bit_xor (
  input  Control,
  input  [33:0] B,
  output [33:0] Result
);

  wire [33:0] bit_extender_1_out;

  assign bit_extender_1_out = {{33{Control}}, Control};  // Bit_Extender bit_extender_1
  assign Result = bit_extender_1_out ^ B;  // XOR_Gate xor_1, 34 bits wide
endmodule

// 34-bit \nADD/SUB
module Add_sub (
  input  Sub,
  input  [33:0] A,
  input  [33:0] B,
  output [33:0] Result,
  output Carry,
  output Overflow
);

  wire and_1_out, and_2_out, l_33th_bit_out_1_l_33th_bit, l_33th_bit_out_2_l_33th_bit,
       l_33th_bit_out_3_l_33th_bit, not_1_out, not_2_out, not_3_out;
  wire [33:0] l_34_bit_xor_1_result;

  L_33th_bit_out l_33th_bit_out_1 (.Input(A), .L_33th_bit(l_33th_bit_out_1_l_33th_bit));
  not not_1 (not_1_out, l_33th_bit_out_1_l_33th_bit);
  L_33th_bit_out l_33th_bit_out_2 (.Input(B), .L_33th_bit(l_33th_bit_out_2_l_33th_bit));
  not not_2 (not_2_out, l_33th_bit_out_2_l_33th_bit);
  L_34_bit_xor l_34_bit_xor_1 (.Control(Sub), .B(B), .Result(l_34_bit_xor_1_result));
  L_34_bit_full_adder_concise l_34_bit_full_adder_concise_1 (
    .A(A), .B(l_34_bit_xor_1_result), .Carry_in_83e99e4a(Sub), .Result(Result), .Carry(Carry));
  L_33th_bit_out l_33th_bit_out_3 (.Input(Result), .L_33th_bit(l_33th_bit_out_3_l_33th_bit));
  not not_3 (not_3_out, l_33th_bit_out_3_l_33th_bit);
  and and_1 (and_1_out, not_3_out, l_33th_bit_out_2_l_33th_bit, l_33th_bit_out_1_l_33th_bit);
  and and_2 (and_2_out, l_33th_bit_out_3_l_33th_bit, not_2_out, not_1_out);
  or or_1 (Overflow, and_1_out, and_2_out);

  // Notes on the sheet:
  //   A33
  //   B33
  //   Result 33
endmodule

// 33th
module L_33th_bit_out (
  input  [33:0] Input,
  output L_33th_bit
);


  assign L_33th_bit = Input[33];
endmodule

// Reduce-OR
module L_34_bit_reduce_or (
  input  [33:0] Input,
  output Output
);

  or or_1 (Output, Input[0], Input[1], Input[2], Input[3], Input[4], Input[5], Input[6], Input[7], Input[8], Input[9], Input[10], Input[11], Input[12], Input[13], Input[14], Input[15], Input[16], Input[18], Input[19], Input[20], Input[21], Input[22], Input[23], Input[24], Input[25], Input[26], Input[27], Input[28], Input[29], Input[30], Input[31], Input[32], Input[33], Input[17]);
endmodule

// 34-bit-ALU
module L_34_bit_ALU (
  input  Control0,
  input  Control1,
  input  control2,
  input  [33:0] A,
  input  [33:0] B,
  output [33:0] Result,
  output Zero,
  output Negative,
  output Overflow,
  output Carry
);

  wire l_34_bit_reduce_or_1_output;
  wire [33:0] add_sub_1_result, comp_1_out_2, l_34_bit_and_1_result, l_34_bit_or_1_result, multiplexer_1_out,
       multiplexer_2_out, multiplexer_3_out, multiplexer_4_out, multiplexer_6_out, r_ol_1_out_2,
       r_or_1_output, x_or_1_output;

  L_34_bit_and l_34_bit_and_1 (.A(A), .B(B), .Result(l_34_bit_and_1_result));
  L_34_bit_OR l_34_bit_or_1 (.A(A), .B(B), .Result(l_34_bit_or_1_result));
  Add_sub add_sub_1 (.B(B), .A(A), .Sub(Control0), .Overflow(Overflow), .Carry(Carry), .Result(add_sub_1_result));
  x_or x_or_1 (.A(A), .B(B), .\output (x_or_1_output));
  R_OL r_ol_1 (.in_1(A), .out_2(r_ol_1_out_2));
  R_OR r_or_1 (.\input (A), .\output (r_or_1_output));
  Comp comp_1 (.in_1(A), .out_2(comp_1_out_2));
  Multiplexer #(.width(34)) multiplexer_1 (
    .in0(l_34_bit_and_1_result), .in1(l_34_bit_or_1_result), .out(multiplexer_1_out), .sel(Control0));
  Multiplexer #(.width(34)) multiplexer_2 (
    .in0(multiplexer_1_out), .in1(add_sub_1_result), .out(multiplexer_2_out), .sel(Control1));
  Multiplexer #(.width(34)) multiplexer_3 (
    .in0(x_or_1_output), .in1(r_ol_1_out_2), .out(multiplexer_3_out), .sel(Control0));
  Multiplexer #(.width(34)) multiplexer_4 (
    .in0(r_or_1_output), .in1(comp_1_out_2), .out(multiplexer_4_out), .sel(Control0));
  Multiplexer #(.width(34)) multiplexer_5 (
    .in0(multiplexer_2_out), .in1(multiplexer_6_out), .out(Result), .sel(control2));
  Multiplexer #(.width(34)) multiplexer_6 (
    .in0(multiplexer_3_out), .in1(multiplexer_4_out), .out(multiplexer_6_out), .sel(Control1));
  L_33th_bit_out l_33th_bit_out_1 (.Input(Result), .L_33th_bit(Negative));
  L_34_bit_reduce_or l_34_bit_reduce_or_1 (.Input(Result), .Output(l_34_bit_reduce_or_1_output));
  not not_1 (Zero, l_34_bit_reduce_or_1_output);
endmodule

module x_or (
  input  [33:0] A,
  input  [33:0] B,
  output [33:0] \output 
);

  assign \output  = A ^ B;  // XOR_Gate xor_1, 34 bits wide
endmodule

module R_OR (
  input  [33:0] \input ,
  output [33:0] \output 
);


  assign \output  = {\input [0], \input [33:1]};
endmodule

module R_OL (
  input  [33:0] in_1,
  output [33:0] out_2
);


  assign out_2 = {in_1[32:0], in_1[33]};
endmodule

module Comp (
  input  [33:0] in_1,
  output [33:0] out_2
);

  wire [33:0] not_1_out;

  assign not_1_out = ~in_1;  // NOT_Gate not_1, 34 bits wide
  L_34_bit_full_adder_concise l_34_bit_full_adder_concise_1 (
    .A(not_1_out), .B(34'h1), .Carry_in_83e99e4a(1'b0), .Result(out_2));  // open: Carry
endmodule
