// Logisim project BOOTHS_MULTIPLICATION.circ as structural Verilog: 2 circuits, main circuit Booth_s_multiplier
module Booth_s_multiplier (
  input  [33:0] M_input,
  input  [33:0] Q_input,
  input  Reset
);

  wire A_out, clock_1_out, controller_1_c0, controller_1_c1, controller_1_cl_a_q_1, controller_1_dec_cnt,
       controller_1_load_a, controller_1_load_m_q_cnt, controller_1_shr, l_34_bit_alu_1_p4, not_1_out,
       Q_1_q0, Q_out, Q_q33;
  wire [5:0] counter_1_q;
  wire [33:0] A_q33, l_34_bit_alu_1_p6, M_q33;

  Clock clock_1 (.out(clock_1_out));
  Controller controller_1 (
    .Clk(clock_1_out), .Reset(Reset), .Q0(Q_q33), .Q_1(Q_1_q0), .Count(counter_1_q),
    .Cl_A_Q_1(controller_1_cl_a_q_1), .LOad_M_Q_Cnt(controller_1_load_m_q_cnt), .Load_A(controller_1_load_a),
    .C0(controller_1_c0), .C1(controller_1_c1), .Shr(controller_1_shr), .Dec_Cnt(controller_1_dec_cnt));
  not not_1 (not_1_out, controller_1_dec_cnt);
  Counter #(.max('h22), .width(6)) counter_1 (
    .load(controller_1_load_m_q_cnt), .D(6'b100010), .count(controller_1_dec_cnt), .Q(counter_1_q),
    .up(not_1_out), .clk(clock_1_out));  // open: carry, clr
  Shift_Register #(.length(34)) M (
    .shift(1'b0), .clk(clock_1_out), .load(controller_1_load_m_q_cnt), .d0(M_input[33]), .q0(M_q33[33]),
    .d1(M_input[32]), .q1(M_q33[32]), .d2(M_input[31]), .q2(M_q33[31]), .d3(M_input[30]), .q3(M_q33[30]),
    .d4(M_input[29]), .q4(M_q33[29]), .d5(M_input[28]), .q5(M_q33[28]), .d6(M_input[27]), .q6(M_q33[27]),
    .d7(M_input[26]), .q7(M_q33[26]), .d8(M_input[25]), .q8(M_q33[25]), .d9(M_input[24]), .q9(M_q33[24]),
    .d10(M_input[23]), .q10(M_q33[23]), .d11(M_input[22]), .q11(M_q33[22]), .d12(M_input[21]),
    .q12(M_q33[21]), .d13(M_input[20]), .q13(M_q33[20]), .d14(M_input[19]), .q14(M_q33[19]),
    .d15(M_input[18]), .q15(M_q33[18]), .d16(M_input[17]), .q16(M_q33[17]), .d17(M_input[16]),
    .q17(M_q33[16]), .d18(M_input[15]), .q18(M_q33[15]), .d19(M_input[14]), .q19(M_q33[14]),
    .d20(M_input[13]), .q20(M_q33[13]), .d21(M_input[12]), .q21(M_q33[12]), .d22(M_input[11]),
    .q22(M_q33[11]), .d23(M_input[10]), .q23(M_q33[10]), .d24(M_input[9]), .q24(M_q33[9]), .d25(M_input[8]),
    .q25(M_q33[8]), .d26(M_input[7]), .q26(M_q33[7]), .d27(M_input[6]), .q27(M_q33[6]), .d28(M_input[5]),
    .q28(M_q33[5]), .d29(M_input[4]), .q29(M_q33[4]), .d30(M_input[3]), .q30(M_q33[3]), .d31(M_input[2]),
    .q31(M_q33[2]), .d32(M_input[1]), .q32(M_q33[1]), .d33(M_input[0]), .q33(M_q33[0]));  // open: in, out, clr
  Shift_Register #(.length(34)) A (
    .shift(controller_1_shr), .in(A_q33[33]), .clk(clock_1_out), .out(A_out), .load(controller_1_load_a),
    .clr(controller_1_cl_a_q_1), .d0(l_34_bit_alu_1_p6[33]), .q0(A_q33[33]), .d1(l_34_bit_alu_1_p6[32]),
    .q1(A_q33[32]), .d2(l_34_bit_alu_1_p6[31]), .q2(A_q33[31]), .d3(l_34_bit_alu_1_p6[30]), .q3(A_q33[30]),
    .d4(l_34_bit_alu_1_p6[29]), .q4(A_q33[29]), .d5(l_34_bit_alu_1_p6[28]), .q5(A_q33[28]),
    .d6(l_34_bit_alu_1_p6[27]), .q6(A_q33[27]), .d7(l_34_bit_alu_1_p6[26]), .q7(A_q33[26]),
    .d8(l_34_bit_alu_1_p6[25]), .q8(A_q33[25]), .d9(l_34_bit_alu_1_p6[24]), .q9(A_q33[24]),
    .d10(l_34_bit_alu_1_p6[23]), .q10(A_q33[23]), .d11(l_34_bit_alu_1_p6[22]), .q11(A_q33[22]),
    .d12(l_34_bit_alu_1_p6[21]), .q12(A_q33[21]), .d13(l_34_bit_alu_1_p6[20]), .q13(A_q33[20]),
    .d14(l_34_bit_alu_1_p6[19]), .q14(A_q33[19]), .d15(l_34_bit_alu_1_p6[18]), .q15(A_q33[18]),
    .d16(l_34_bit_alu_1_p6[17]), .q16(A_q33[17]), .d17(l_34_bit_alu_1_p6[16]), .q17(A_q33[16]),
    .d18(l_34_bit_alu_1_p6[15]), .q18(A_q33[15]), .d19(l_34_bit_alu_1_p6[14]), .q19(A_q33[14]),
    .d20(l_34_bit_alu_1_p6[13]), .q20(A_q33[13]), .d21(l_34_bit_alu_1_p6[12]), .q21(A_q33[12]),
    .d22(l_34_bit_alu_1_p6[11]), .q22(A_q33[11]), .d23(l_34_bit_alu_1_p6[10]), .q23(A_q33[10]),
    .d24(l_34_bit_alu_1_p6[9]), .q24(A_q33[9]), .d25(l_34_bit_alu_1_p6[8]), .q25(A_q33[8]),
    .d26(l_34_bit_alu_1_p6[7]), .q26(A_q33[7]), .d27(l_34_bit_alu_1_p6[6]), .q27(A_q33[6]),
    .d28(l_34_bit_alu_1_p6[5]), .q28(A_q33[5]), .d29(l_34_bit_alu_1_p6[4]), .q29(A_q33[4]),
    .d30(l_34_bit_alu_1_p6[3]), .q30(A_q33[3]), .d31(l_34_bit_alu_1_p6[2]), .q31(A_q33[2]),
    .d32(l_34_bit_alu_1_p6[1]), .q32(A_q33[1]), .d33(l_34_bit_alu_1_p6[0]), .q33(A_q33[0]));
  Shift_Register #(.length(34)) Q (
    .shift(controller_1_shr), .in(A_out), .clk(clock_1_out), .out(Q_out), .load(controller_1_load_m_q_cnt),
    .d0(Q_input[33]), .d1(Q_input[32]), .d2(Q_input[31]), .d3(Q_input[30]), .d4(Q_input[29]),
    .d5(Q_input[28]), .d6(Q_input[27]), .d7(Q_input[26]), .d8(Q_input[25]), .d9(Q_input[24]),
    .d10(Q_input[23]), .d11(Q_input[22]), .d12(Q_input[21]), .d13(Q_input[20]), .d14(Q_input[19]),
    .d15(Q_input[18]), .d16(Q_input[17]), .d17(Q_input[16]), .d18(Q_input[15]), .d19(Q_input[14]),
    .d20(Q_input[13]), .d21(Q_input[12]), .d22(Q_input[11]), .d23(Q_input[10]), .d24(Q_input[9]),
    .d25(Q_input[8]), .d26(Q_input[7]), .d27(Q_input[6]), .d28(Q_input[5]), .d29(Q_input[4]),
    .d30(Q_input[3]), .d31(Q_input[2]), .d32(Q_input[1]), .d33(Q_input[0]), .q33(Q_q33));  // open: clr, q0, q1, q2, q3, q4, q5, q6, q7, q8, q9, q10, q11, q12, q13, q14, q15, q16, q17, q18, q19, q20, q21, q22, q23, q24, q25, q26, q27, q28, q29, q30, q31, q32
  // L_34_bit_ALU l_34_bit_alu_1: pin names not known; wires that end beside it: A_q33, M_q33, controller_1_c1, l_34_bit_alu_1_p4, controller_1_c0, l_34_bit_alu_1_p6, 1'b0, l_34_bit_alu_1_p4
  Shift_Register #(.length(1)) Q_1 (
    .shift(controller_1_shr), .in(Q_out), .clk(clock_1_out), .clr(controller_1_cl_a_q_1), .q0(Q_1_q0));  // open: out, load, d0
endmodule

// Control \nUnit
module Controller (
  input  Clk,
  input  Reset,
  input  Q0,
  input  Q_1,
  input  [5:0] Count,
  output Cl_A_Q_1,
  output LOad_M_Q_Cnt,
  output Load_A,
  output C0,
  output C1,
  output Shr,
  output Dec_Cnt
);

  wire and_3_out, and_4_out, multiplexer_1_out, not_1_out, not_2_out, not_3_out, not_4_out, not_5_out,
       not_6_out, not_7_out, or_2_out, Q0_Q_1_out;
  wire [1:0] rom_1_data_2;
  wire [2:0] and_1_out, and_2_out, bit_extender_1_out, bit_extender_2_out, bit_extender_3_out, CAR_q,
       or_1_out, rom_1_data;

  assign bit_extender_1_out = {{2{Q0_Q_1_out}}, Q0_Q_1_out};  // Bit_Extender bit_extender_1
  and Q0_Q_1 (Q0_Q_1_out, not_2_out, Q_1);
  not not_1 (not_1_out, Q0_Q_1_out);
  assign bit_extender_2_out = {{2{not_1_out}}, not_1_out};  // Bit_Extender bit_extender_2
  assign and_1_out = 3'b100 & bit_extender_3_out & bit_extender_1_out;  // AND_Gate and_1, 3 bits wide
  assign or_1_out = and_1_out | rom_1_data | and_2_out;  // OR_Gate or_1, 3 bits wide
  not not_2 (not_2_out, Q0);
  assign and_2_out = bit_extender_2_out & bit_extender_3_out & 3'b101;  // AND_Gate and_2, 3 bits wide
  assign bit_extender_3_out = {{2{and_3_out}}, and_3_out};  // Bit_Extender bit_extender_3
  and and_3 (and_3_out, not_3_out, CAR_q[1], not_4_out);
  not not_3 (not_3_out, CAR_q[2]);
  not not_4 (not_4_out, CAR_q[0]);
  Counter #(.max('h7), .width(3)) CAR (
    .load(not_5_out), .D(or_1_out), .count(multiplexer_1_out), .Q(CAR_q), .up(1'b1), .clk(Clk), .clr(Reset));  // open: carry
  not not_5 (not_5_out, multiplexer_1_out);
  Multiplexer #(.select(2)) multiplexer_1 (
    .in0(1'b0), .in1(1'b1), .in2(and_4_out), .in3(not_7_out), .out(multiplexer_1_out), .sel(rom_1_data_2));
  and and_4 (and_4_out, not_6_out, Q0);
  not not_6 (not_6_out, Q_1);
  not not_7 (not_7_out, or_2_out);
  or or_2 (or_2_out, Count[0], Count[1], Count[2], Count[3], Count[4], Count[5]);
  ROM #(.addrWidth(3), .dataWidth(12)) rom_1 (
    .addr(CAR_q), .data({Cl_A_Q_1, LOad_M_Q_Cnt, Load_A, C0, C1, Shr, Dec_Cnt, rom_1_data, rom_1_data_2}));

  // Notes on the sheet:
  //   To choose only
  //   state 2 (010)
  //   Control Word Format: Clear (A, Q-1), Load (M, Q, Cnt), Load A, C0, C1, Shr, Dec Cnt, Address bits (3 bit), Selection bits (2 bit)
  //   contents of rom_1 (hex, n*v repeats v):
  //   1 c01 2 394 281 61 b 1c
endmodule
