// Logisim project CACHE.circ as structural Verilog: 1 circuit, main circuit cache
module cache (
  input  Reset,
  input  [3:0] Addr,
  input  store,
  input  clk,
  input  load,
  input  [33:0] \input ,
  output Hit,
  output Miss,
  output [33:0] DataOut
);

  wire and_1_out, comparator_1_eq, comparator_2_eq, comparator_3_eq, comparator_4_eq, decoder_1_out0,
       decoder_1_out1, decoder_1_out2, decoder_1_out3, or_1_out;
  wire [2:0] register_1_q, register_3_q, register_5_q, register_7_q;
  wire [33:0] multiplexer_1_out, multiplexer_3_out, RAM_DATA, register_2_q, register_4_q, register_6_q,
       register_8_q;

  RAM #(.addrWidth(4), .asyncread("true"), .dataWidth(34), .databus("bibusControlled")) ram_1 (
    .addr(Addr), .we(store), .oe(load), .clk(clk), .din(\input ), .dout(RAM_DATA));
  or or_1 (or_1_out, store, and_1_out);
  and and_1 (and_1_out, Miss, load);
  Decoder #(.select(2)) decoder_1 (
    .out0(decoder_1_out0), .out1(decoder_1_out1), .out2(decoder_1_out2), .out3(decoder_1_out3),
    .sel(Addr[1:0]), .en(or_1_out));
  Multiplexer #(.width(34)) multiplexer_1 (.in0(RAM_DATA), .in1(\input ), .out(multiplexer_1_out), .sel(store));
  Register #(.width(3)) register_1 (
    .D({1'b1, Addr[3:2]}), .en(decoder_1_out0), .Q(register_1_q), .clk(clk), .clr(Reset));
  Register #(.width(34)) register_2 (
    .D(multiplexer_1_out), .en(decoder_1_out0), .Q(register_2_q), .clk(clk));  // open: clr
  Register #(.width(3)) register_3 (
    .D({1'b1, Addr[3:2]}), .en(decoder_1_out1), .Q(register_3_q), .clk(clk), .clr(Reset));
  Register #(.width(34)) register_4 (
    .D(multiplexer_1_out), .en(decoder_1_out1), .Q(register_4_q), .clk(clk));  // open: clr
  Register #(.width(3)) register_5 (
    .D({1'b1, Addr[3:2]}), .en(decoder_1_out2), .Q(register_5_q), .clk(clk), .clr(Reset));
  Register #(.width(34)) register_6 (
    .D(multiplexer_1_out), .en(decoder_1_out2), .Q(register_6_q), .clk(clk));  // open: clr
  Register #(.width(3)) register_7 (
    .D({1'b1, Addr[3:2]}), .en(decoder_1_out3), .Q(register_7_q), .clk(clk), .clr(Reset));
  Register #(.width(34)) register_8 (
    .D(multiplexer_1_out), .en(decoder_1_out3), .Q(register_8_q), .clk(clk));  // open: clr
  Comparator #(.width(3)) comparator_1 (.a({1'b1, Addr[3:2]}), .b(register_1_q), .eq(comparator_1_eq));  // open: gt, lt
  Comparator #(.width(3)) comparator_2 (.a({1'b1, Addr[3:2]}), .b(register_3_q), .eq(comparator_2_eq));  // open: gt, lt
  Comparator #(.width(3)) comparator_3 (.a({1'b1, Addr[3:2]}), .b(register_5_q), .eq(comparator_3_eq));  // open: gt, lt
  Comparator #(.width(3)) comparator_4 (.a({1'b1, Addr[3:2]}), .b(register_7_q), .eq(comparator_4_eq));  // open: gt, lt
  Multiplexer #(.select(2)) multiplexer_2 (
    .in0(comparator_1_eq), .in1(comparator_2_eq), .in2(comparator_3_eq), .in3(comparator_4_eq), .out(Hit),
    .sel(Addr[1:0]));
  Multiplexer #(.select(2), .width(34)) multiplexer_3 (
    .in0(register_2_q), .in1(register_4_q), .in2(register_6_q), .in3(register_8_q), .out(multiplexer_3_out),
    .sel(Addr[1:0]));
  not not_1 (Miss, Hit);
  Multiplexer #(.width(34)) multiplexer_4 (.in0(multiplexer_3_out), .in1(RAM_DATA), .out(DataOut), .sel(Miss));

  // Other names for the same wires on the sheet: Idx[1:0] = Addr[1:0]; LoadCtl = load; RawMiss = Miss;
  //   StoreCtl = store

  // Notes on the sheet:
  //   Direct-mapped cache: 4 lines x 1 word (34-bit data, 16 x 34 backing RAM). Addr = tag[3:2] | index[1:0]
  //   Each line = 3-bit {valid,tag} register + 34-bit data register. Hit = stored {valid,tag} == current {1,tag}
  //   Read miss: RAM data bypasses to DataOut and fills selected line. Store: write-through RAM + update selected cache line.
endmodule
