// Logisim project CPU.circ as structural Verilog: 4 circuits, main circuit main
module main (
  input  req_inter
);

  wire clock_1_out, cpu_1_initizalization, cpu_1_r, cpu_1_w, multiplexer_1_out, or_1_out, register_1_q,
       Reset_out;
  wire [3:0] cpu_1_addr;
  wire [33:0] cachee_dataout, cpu_1_dataout;

  Clock clock_1 (.out(clock_1_out));
  Button Reset (.out(Reset_out));
  Multiplexer multiplexer_1 (.in0(or_1_out), .in1(1'b0), .out(multiplexer_1_out), .sel(cpu_1_initizalization));
  or or_1 (or_1_out, req_inter, register_1_q);
  Register #(.width(1)) register_1 (
    .D(multiplexer_1_out), .Q(register_1_q), .clk(clock_1_out), .clr(Reset_out));  // open: en
  CPU cpu_1 (
    .Clk(clock_1_out), .Reset(Reset_out), .waiting_in(register_1_q), .R(cpu_1_r), .W(cpu_1_w),
    .Addr(cpu_1_addr), .DataIn(cachee_dataout), .DataOut(cpu_1_dataout),
    .initizalization(cpu_1_initizalization));
  cache cachee (
    .store(cpu_1_w), .clk(clock_1_out), .load(cpu_1_r), .Reset(Reset_out), .\input (cpu_1_dataout),
    .Addr(cpu_1_addr), .DataOut(cachee_dataout));  // open: Hit, Miss

  // Notes on the sheet:
  //   0 - AND
  //   1 - ADD
  //   2 - STO
  //   3 - OR
  //   4 - SUB
  //   5 - BUN
  //   6 - LDA
  //   7 - HLT
endmodule

module CPU (
  input  Clk,
  input  Reset,
  input  [33:0] DataIn,
  input  waiting_in,
  output R,
  output W,
  output [3:0] Addr,
  output [33:0] DataOut,
  output initizalization
);

  wire b1, c0, c1, c2alu, controlunit_1_c1, controlunit_1_c2, controlunit_1_car_at_zero, d1, d2,
       interrupt_1_finished, LdA, LdA_from_MBR_d0c4dcbb, LoadAc, LoadB, LoadMAR, or_1_out, or_2_out, or_3_out;
  wire [3:0] interrupt_1_stored_pc_out, multiplexer_1_out, multiplexer_2_out, multiplexer_3_out, PC_q;
  wire [33:0] Ac, AcIn, ALUout, interrupt_1_ac_d, multiplexer_4_out;

  Multiplexer #(.width(4)) multiplexer_1 (
    .in0(DataOut[3:0]), .in1(4'b1010), .out(multiplexer_1_out), .sel(initizalization));
  Multiplexer #(.width(4)) multiplexer_2 (
    .in0(multiplexer_1_out), .in1(interrupt_1_stored_pc_out), .out(multiplexer_2_out),
    .sel(interrupt_1_finished));
  or or_1 (or_1_out, controlunit_1_c2, initizalization, interrupt_1_finished);
  Multiplexer #(.width(4)) multiplexer_3 (.in0(PC_q), .in1(DataOut[3:0]), .out(multiplexer_3_out), .sel(d2));
  ControlUnit controlunit_1 (
    .IR(DataOut[7:4]), .Clk(Clk), .Reset(Reset), .holding(or_2_out), .LoadAc(LdA), .Operation({c0, c1}),
    .c2alu(c2alu), .car_at_zero(controlunit_1_car_at_zero), .d1(d1), .R(R), .d2(d2), .c2(controlunit_1_c2),
    .b1(b1), .W(W), .LdAfrB(LdA_from_MBR_d0c4dcbb), .c1(controlunit_1_c1));  // open: b3, b2
  or or_2 (or_2_out, initizalization, interrupt_1_finished);
  interrupt interrupt_1 (
    .CLK(Clk), .RESET(Reset), .PC_Q(PC_q), .WAITING_IN(waiting_in), .CAR_AT_ZERO(controlunit_1_car_at_zero),
    .AC_OUT(Ac), .AC_IN(AcIn), .INITIALIZATION(initizalization), .FINISHED(interrupt_1_finished),
    .STORED_PC_OUT(interrupt_1_stored_pc_out), .AC_D(interrupt_1_ac_d));  // open: BUSY_OUT
  Counter #(.max('hf), .width(4)) PC (
    .load(or_1_out), .D(multiplexer_2_out), .count(controlunit_1_c1), .Q(PC_q), .clk(Clk), .clr(Reset));  // open: carry, up
  Register #(.width(4)) MAR (.D(multiplexer_3_out), .en(LoadMAR), .Q(Addr), .clk(Clk), .clr(Reset));
  Register #(.width(4)) IR (.D(DataOut[7:4]), .en(controlunit_1_c1), .clk(Clk), .clr(Reset));  // open: Q
  Multiplexer #(.width(34)) multiplexer_4 (.in0(DataIn), .in1(Ac), .out(multiplexer_4_out), .sel(b1));
  or or_3 (or_3_out, LoadAc, interrupt_1_finished);
  Register #(.width(34)) MBR (.D(multiplexer_4_out), .en(LoadB), .Q(DataOut), .clk(Clk), .clr(Reset));
  Register #(.width(34)) u_Ac (.D(interrupt_1_ac_d), .en(or_3_out), .Q(Ac), .clk(Clk), .clr(Reset));
  ALU34_CPU alu34_cpu_1 (.A(Ac), .B(DataOut), .c1(c1), .c0(c0), .c2(c2alu), .Result(ALUout));
  or or_4 (LoadMAR, d1, d2);
  or or_5 (LoadB, R, b1);
  Multiplexer #(.width(34)) multiplexer_5 (.in0(ALUout), .in1(DataOut), .out(AcIn), .sel(LdA_from_MBR_d0c4dcbb));
  or or_6 (LoadAc, LdA_from_MBR_d0c4dcbb, LdA);

  // Other names for the same wires on the sheet: clr = Reset; MBRout[33:0] = DataOut
endmodule

// ALU 34
module ALU34_CPU (
  input  c1,
  input  c0,
  input  c2,
  input  [33:0] A,
  input  [33:0] B,
  output [33:0] Result
);

  L_34_bit_ALU l_34_bit_alu_1 (
    .A(A), .B(B), .Control0(c0), .Control1(c1), .control2(c2), .Result(Result));  // open: Zero, Negative, Overflow, Carry
endmodule

// CU
module ControlUnit (
  input  [3:0] IR,
  input  Clk,
  input  Reset,
  input  holding,
  output c1,
  output d1,
  output R,
  output d2,
  output c2,
  output [1:0] Operation,
  output b1,
  output LoadAc,
  output W,
  output b3,
  output b2,
  output LdAfrB,
  output c2alu,
  output car_at_zero
);

  wire and_1_out, decoder_1_out6, decoder_1_out7, decoder_1_out8, decoder_1_out9, decoder_1_out15, not_1_out,
       not_2_out, or_1_out;
  wire [4:0] CAR_BUS_C2;
  wire [6:0] rom_1_data;

  ROM #(.addrWidth(6), .dataWidth(7)) rom_1 (.addr({c2alu, CAR_BUS_C2}), .data(rom_1_data));
  not not_1 (not_1_out, rom_1_data[0]);
  Counter #(.max('h3f), .width(6)) counter_1 (
    .load(rom_1_data[2]), .D({IR, 2'b11}), .count(rom_1_data[0]), .Q({c2alu, CAR_BUS_C2}), .clk(and_1_out),
    .clr(or_1_out));  // open: carry, up
  or or_1 (or_1_out, rom_1_data[1], holding, Reset);
  and and_1 (and_1_out, Clk, not_2_out);
  not not_2 (not_2_out, decoder_1_out15);
  Decoder #(.enable("false"), .select(4)) decoder_1 (
    .out1(d1), .out2(c1), .out3(R), .out4(c2), .out5(d2), .out6(decoder_1_out6), .out7(decoder_1_out7),
    .out8(decoder_1_out8), .out9(decoder_1_out9), .out10(b1), .out11(W), .out12(b2), .out13(b3),
    .out14(LdAfrB), .out15(decoder_1_out15), .sel(rom_1_data[6:3]));  // open: out0
  Comparator #(.width(6)) comparator_1 (.a({c2alu, CAR_BUS_C2}), .b({6{1'b0}}), .eq(car_at_zero));  // open: gt, lt
  Priority_Encoder #(.select(2)) priority_encoder_1 (
    .in0(decoder_1_out6), .in1(decoder_1_out7), .in2(decoder_1_out8), .in3(decoder_1_out9), .out(Operation),
    .en_in(LoadAc));  // open: gs, en_out
  or or_2 (LoadAc, decoder_1_out6, decoder_1_out7, decoder_1_out8, decoder_1_out9);

  // Other names for the same wires on the sheet: CAR_BUS_C2[5] = c2alu

  // Notes on the sheet:
  //   contents of rom_1 (hex, n*v repeats v):
  //   9 19 14 29 19 31 2 29 19 39 2 29 51 59 2 29 19 41 2 29 19 49 2 21 2 2 2 29 19 71 2 78 9 19 14 29 19
  //   31 2 29 19 41 2 29 19 39 2 29 19 49 2 13*78
endmodule
