// Logisim project DIVISION.circ as structural Verilog: 1 circuit, main circuit main
module main (
  input  start,
  input  [33:0] dividend,
  input  [33:0] divisor,
  output [33:0] quotient,
  output [33:0] remainder,
  output done
);

  wire adder_1_cout, adder_2_cout, and_1_out, and_2_out, and_3_out, and_4_out, busy_flag_353100ca_q,
       clock_1_out, comparator_1_eq, not_1_out, not_2_out, not_3_out, not_4_out, or_1_out, or_2_out,
       or_3_out, or_4_out, subtractor_1_bout;
  wire [5:0] adder_4_out, count_q, multiplexer_4_out;
  wire [33:0] adder_2_out, adder_3_out, multiplexer_1_out, multiplexer_2_out, multiplexer_3_out,
       register_3_q, subtractor_1_out;

  Clock clock_1 (.out(clock_1_out));
  not not_1 (not_1_out, busy_flag_353100ca_q);
  Adder #(.width(34)) adder_1 (.a(quotient), .b(quotient), .cout(adder_1_cout));  // open: out, cin
  Multiplexer #(.width(34)) multiplexer_1 (
    .in0(adder_2_out), .in1(subtractor_1_out), .out(multiplexer_1_out), .sel(or_4_out));
  Register #(.width(34)) register_1 (
    .D(multiplexer_3_out), .en(or_1_out), .clk(clock_1_out), .Q(quotient));  // open: clr
  and and_1 (and_1_out, start, not_1_out);
  and and_2 (and_2_out, busy_flag_353100ca_q, comparator_1_eq);
  or or_1 (or_1_out, and_1_out, busy_flag_353100ca_q);
  not not_2 (not_2_out, and_1_out);
  Adder #(.width(34)) adder_2 (
    .a(remainder), .b(remainder), .out(adder_2_out), .cin(adder_1_cout), .cout(adder_2_cout));
  Multiplexer #(.width(34)) multiplexer_2 (
    .in0(multiplexer_1_out), .in1({34{1'b0}}), .out(multiplexer_2_out), .sel(and_1_out));
  Register #(.width(34)) register_2 (
    .D(multiplexer_2_out), .en(or_1_out), .clk(clock_1_out), .Q(remainder));  // open: clr
  not not_3 (not_3_out, comparator_1_eq);
  and and_3 (and_3_out, done, not_2_out);
  Subtractor #(.width(34)) subtractor_1 (
    .a(adder_2_out), .b(register_3_q), .out(subtractor_1_out), .bout(subtractor_1_bout));  // open: bin
  Adder #(.width(34)) adder_3 (.a(quotient), .b(quotient), .out(adder_3_out), .cin(or_4_out));  // open: cout
  Register #(.width(34)) register_3 (.D(divisor), .en(and_1_out), .clk(clock_1_out), .Q(register_3_q));  // open: clr
  and and_4 (and_4_out, busy_flag_353100ca_q, not_3_out);
  or or_2 (or_2_out, and_2_out, and_3_out);
  not not_4 (not_4_out, subtractor_1_bout);
  or or_3 (or_3_out, and_1_out, and_4_out);
  Multiplexer #(.width(34)) multiplexer_3 (.in0(adder_3_out), .in1(dividend), .out(multiplexer_3_out), .sel(and_1_out));
  Register #(.width(6)) count (.D(multiplexer_4_out), .en(or_1_out), .clk(clock_1_out), .Q(count_q));  // open: clr
  or or_4 (or_4_out, adder_2_cout, not_4_out);
  Adder #(.width(6)) adder_4 (.a(count_q), .b({6{1'b1}}), .out(adder_4_out));  // open: cin, cout
  Register #(.width(1)) busy_flag_353100ca (
    .D(or_3_out), .clk(clock_1_out), .Q(busy_flag_353100ca_q));  // open: en, clr
  Multiplexer #(.width(6)) multiplexer_4 (.in0(adder_4_out), .in1(6'b100010), .out(multiplexer_4_out), .sel(and_1_out));
  Register #(.width(1)) done_flag_3ebbcef8 (.D(or_2_out), .clk(clock_1_out), .Q(done));  // open: en, clr
  Comparator #(.width(6)) comparator_1 (.a(count_q), .b(6'b000001), .eq(comparator_1_eq));  // open: gt, lt

  // Notes on the sheet:
  //   34-bit sequential restoring divider.  Pulse start for 1 clock, then keep clocking: done=1 after 34 clocks.
  //   REGISTERS
  //   CONTROL: load = start AND NOT busy;  busy runs for 34 clocks;  done set at the end
  //   Outputs
endmodule
