// Logisim project ECC.circ as structural Verilog
module encode (
  input  [33:0] pin_in,
  output [39:0] pin_out
);

  xor xor_1 (pin_out[0], pin_in[0], pin_in[11], pin_in[3], pin_in[4], pin_in[8], pin_in[10], pin_in[13], pin_in[15], pin_in[17], pin_in[19], pin_in[21], pin_in[23], pin_in[25], pin_in[26], pin_in[28], pin_in[30], pin_in[32], pin_in[6], pin_in[1]);
  xor xor_2 (pin_out[1], pin_in[0], pin_in[2], pin_in[3], pin_in[5], pin_in[6], pin_in[9], pin_in[10], pin_in[12], pin_in[13], pin_in[16], pin_in[17], pin_in[20], pin_in[21], pin_in[24], pin_in[25], pin_in[27], pin_in[31], pin_in[32], pin_in[28]);
  xor xor_3 (pin_out[3], pin_in[1], pin_in[2], pin_in[3], pin_in[7], pin_in[8], pin_in[9], pin_in[10], pin_in[14], pin_in[15], pin_in[16], pin_in[17], pin_in[22], pin_in[24], pin_in[23], pin_in[25], pin_in[29], pin_in[30], pin_in[31], pin_in[32]);
  xor xor_4 (pin_out[7], pin_in[25], pin_in[4], pin_in[5], pin_in[6], pin_in[7], pin_in[8], pin_in[9], pin_in[10], pin_in[18], pin_in[19], pin_in[20], pin_in[21], pin_in[22], pin_in[23], pin_in[24], pin_in[33]);
  xor xor_5 (pin_out[15], pin_in[11], pin_in[12], pin_in[13], pin_in[14], pin_in[15], pin_in[16], pin_in[17], pin_in[18], pin_in[24], pin_in[19], pin_in[20], pin_in[21], pin_in[22], pin_in[23], pin_in[25]);
  xor xor_6 (pin_out[31], pin_in[26], pin_in[27], pin_in[28], pin_in[29], pin_in[30], pin_in[31], pin_in[32], pin_in[33]);

  assign {pin_out[39:32], pin_out[30:16], pin_out[14:8], pin_out[6:4], pin_out[2]} = {pin_in[33:27], pin_in[22], pin_in[23], pin_in[25], pin_in[26], pin_in[24], pin_in[21:0]};
endmodule

module decode (
  input  [39:0] data_in,
  output [33:0] data_out,
  output error_detected
);

  wire decoder_1_out3, decoder_1_out5, decoder_1_out6, decoder_1_out7, decoder_1_out9, decoder_1_out10,
       decoder_1_out11, decoder_1_out12, decoder_1_out13, decoder_1_out14, decoder_1_out15, decoder_1_out17,
       decoder_1_out18, decoder_1_out19, decoder_1_out20, decoder_1_out21, decoder_1_out22, decoder_1_out23,
       decoder_1_out24, decoder_1_out25, decoder_1_out26, decoder_1_out27, decoder_1_out28, decoder_1_out29,
       decoder_1_out30, decoder_1_out31, decoder_1_out33, decoder_1_out34, decoder_1_out35, decoder_1_out36,
       decoder_1_out37, decoder_1_out38, decoder_1_out39, decoder_1_out40, not_1_out, not_2_out, not_3_out,
       not_4_out, not_5_out, not_6_out, not_7_out, not_8_out, not_9_out, not_10_out, not_11_out, not_12_out,
       not_13_out, not_14_out, not_15_out, not_16_out, not_17_out, not_18_out, not_19_out, not_20_out,
       not_21_out, not_22_out, not_23_out, not_24_out, not_25_out, not_26_out, not_27_out, not_28_out,
       not_29_out, not_30_out, not_31_out, not_32_out, not_33_out, not_34_out, p0, p1, p2, p3, p4, p5;

  xor xor_1 (p0, data_in[0], data_in[2], data_in[4], data_in[6], data_in[8], data_in[10], data_in[12], data_in[14], data_in[16], data_in[18], data_in[20], data_in[22], data_in[24], data_in[26], data_in[28], data_in[30], data_in[32], data_in[34], data_in[36], data_in[38]);
  xor xor_2 (p1, data_in[1], data_in[2], data_in[5], data_in[6], data_in[9], data_in[10], data_in[13], data_in[14], data_in[17], data_in[18], data_in[21], data_in[22], data_in[25], data_in[26], data_in[29], data_in[30], data_in[33], data_in[34], data_in[37], data_in[38]);
  xor xor_3 (p2, data_in[3], data_in[4], data_in[5], data_in[6], data_in[11], data_in[12], data_in[13], data_in[14], data_in[19], data_in[20], data_in[22], data_in[21], data_in[27], data_in[28], data_in[29], data_in[30], data_in[35], data_in[36], data_in[37], data_in[38]);
  xor xor_4 (p3, data_in[9], data_in[10], data_in[11], data_in[12], data_in[13], data_in[14], data_in[23], data_in[24], data_in[25], data_in[26], data_in[27], data_in[28], data_in[29], data_in[30], data_in[7], data_in[8]);
  xor xor_5 (p4, data_in[15], data_in[16], data_in[17], data_in[18], data_in[19], data_in[20], data_in[21], data_in[22], data_in[23], data_in[24], data_in[25], data_in[26], data_in[27], data_in[28], data_in[29], data_in[30]);
  xor xor_6 (p5, data_in[31], data_in[32], data_in[33], data_in[34], data_in[35], data_in[36], data_in[37], data_in[38], data_in[39]);
  or or_1 (error_detected, p0, p1, p2, p3, p4, p5);
  Decoder #(.select(6)) decoder_1 (
    .out3(decoder_1_out3), .out5(decoder_1_out5), .out6(decoder_1_out6), .out7(decoder_1_out7),
    .out9(decoder_1_out9), .out10(decoder_1_out10), .out11(decoder_1_out11), .out12(decoder_1_out12),
    .out13(decoder_1_out13), .out14(decoder_1_out14), .out15(decoder_1_out15), .out17(decoder_1_out17),
    .out18(decoder_1_out18), .out19(decoder_1_out19), .out20(decoder_1_out20), .out21(decoder_1_out21),
    .out22(decoder_1_out22), .out23(decoder_1_out23), .out24(decoder_1_out24), .out25(decoder_1_out25),
    .out26(decoder_1_out26), .out27(decoder_1_out27), .out28(decoder_1_out28), .out29(decoder_1_out29),
    .out30(decoder_1_out30), .out31(decoder_1_out31), .out33(decoder_1_out33), .out34(decoder_1_out34),
    .out35(decoder_1_out35), .out36(decoder_1_out36), .out37(decoder_1_out37), .out38(decoder_1_out38),
    .out39(decoder_1_out39), .out40(decoder_1_out40), .sel({p5, p4, p3, p2, p1, p0}));  // open: out0, out1, out2, out4, out8, out16, out32, out41, out42, out43, out44, out45, out46, out47, out48, out49, out50, out51, out52, out53, out54, out55, out56, out57, out58, out59, out60, out61, out62, out63, en
  not not_1 (not_1_out, data_in[2]);
  not not_2 (not_2_out, data_in[4]);
  not not_3 (not_3_out, data_in[5]);
  not not_4 (not_4_out, data_in[6]);
  not not_5 (not_5_out, data_in[10]);
  not not_6 (not_6_out, data_in[12]);
  not not_7 (not_7_out, data_in[13]);
  not not_8 (not_8_out, data_in[14]);
  not not_9 (not_9_out, data_in[16]);
  not not_10 (not_10_out, data_in[18]);
  not not_11 (not_11_out, data_in[19]);
  not not_12 (not_12_out, data_in[20]);
  Multiplexer multiplexer_1 (.in0(data_in[2]), .in1(not_1_out), .out(data_out[0]), .sel(decoder_1_out3));
  Multiplexer multiplexer_2 (.in0(data_in[4]), .in1(not_2_out), .out(data_out[1]), .sel(decoder_1_out5));
  Multiplexer multiplexer_3 (.in0(data_in[5]), .in1(not_3_out), .out(data_out[2]), .sel(decoder_1_out6));
  Multiplexer multiplexer_4 (.in0(data_in[6]), .in1(not_4_out), .out(data_out[3]), .sel(decoder_1_out7));
  Multiplexer multiplexer_5 (.in0(data_in[8]), .in1(not_13_out), .out(data_out[4]), .sel(decoder_1_out9));
  not not_13 (not_13_out, data_in[8]);
  Multiplexer multiplexer_6 (.in0(data_in[9]), .in1(not_14_out), .out(data_out[5]), .sel(decoder_1_out10));
  not not_14 (not_14_out, data_in[9]);
  Multiplexer multiplexer_7 (.in0(data_in[10]), .in1(not_5_out), .out(data_out[6]), .sel(decoder_1_out11));
  Multiplexer multiplexer_8 (.in0(data_in[11]), .in1(not_15_out), .out(data_out[7]), .sel(decoder_1_out12));
  not not_15 (not_15_out, data_in[11]);
  Multiplexer multiplexer_9 (.in0(data_in[12]), .in1(not_6_out), .out(data_out[8]), .sel(decoder_1_out13));
  Multiplexer multiplexer_10 (.in0(data_in[13]), .in1(not_7_out), .out(data_out[9]), .sel(decoder_1_out14));
  Multiplexer multiplexer_11 (.in0(data_in[14]), .in1(not_8_out), .out(data_out[10]), .sel(decoder_1_out15));
  Multiplexer multiplexer_12 (.in0(data_in[16]), .in1(not_9_out), .out(data_out[11]), .sel(decoder_1_out17));
  Multiplexer multiplexer_13 (.in0(data_in[17]), .in1(not_16_out), .out(data_out[12]), .sel(decoder_1_out18));
  not not_16 (not_16_out, data_in[17]);
  Multiplexer multiplexer_14 (.in0(data_in[18]), .in1(not_10_out), .out(data_out[13]), .sel(decoder_1_out19));
  Multiplexer multiplexer_15 (.in0(data_in[19]), .in1(not_11_out), .out(data_out[14]), .sel(decoder_1_out20));
  Multiplexer multiplexer_16 (.in0(data_in[20]), .in1(not_12_out), .out(data_out[15]), .sel(decoder_1_out21));
  Multiplexer multiplexer_17 (.in0(data_in[21]), .in1(not_17_out), .out(data_out[16]), .sel(decoder_1_out22));
  not not_17 (not_17_out, data_in[21]);
  not not_18 (not_18_out, data_in[22]);
  not not_19 (not_19_out, data_in[23]);
  not not_20 (not_20_out, data_in[24]);
  not not_21 (not_21_out, data_in[25]);
  not not_22 (not_22_out, data_in[26]);
  not not_23 (not_23_out, data_in[27]);
  Multiplexer multiplexer_18 (.in0(data_in[22]), .in1(not_18_out), .out(data_out[17]), .sel(decoder_1_out23));
  Multiplexer multiplexer_19 (.in0(data_in[23]), .in1(not_19_out), .out(data_out[18]), .sel(decoder_1_out24));
  Multiplexer multiplexer_20 (.in0(data_in[24]), .in1(not_20_out), .out(data_out[19]), .sel(decoder_1_out25));
  Multiplexer multiplexer_21 (.in0(data_in[25]), .in1(not_21_out), .out(data_out[20]), .sel(decoder_1_out26));
  Multiplexer multiplexer_22 (.in0(data_in[26]), .in1(not_22_out), .out(data_out[21]), .sel(decoder_1_out27));
  Multiplexer multiplexer_23 (.in0(data_in[27]), .in1(not_23_out), .out(data_out[22]), .sel(decoder_1_out28));
  Multiplexer multiplexer_24 (.in0(data_in[28]), .in1(not_24_out), .out(data_out[23]), .sel(decoder_1_out29));
  not not_24 (not_24_out, data_in[28]);
  Multiplexer multiplexer_25 (.in0(data_in[29]), .in1(not_25_out), .out(data_out[24]), .sel(decoder_1_out30));
  not not_25 (not_25_out, data_in[29]);
  not not_26 (not_26_out, data_in[30]);
  not not_27 (not_27_out, data_in[32]);
  not not_28 (not_28_out, data_in[33]);
  not not_29 (not_29_out, data_in[34]);
  not not_30 (not_30_out, data_in[35]);
  not not_31 (not_31_out, data_in[36]);
  not not_32 (not_32_out, data_in[37]);
  not not_33 (not_33_out, data_in[38]);
  not not_34 (not_34_out, data_in[39]);
  Multiplexer multiplexer_26 (.in0(data_in[30]), .in1(not_26_out), .out(data_out[25]), .sel(decoder_1_out31));
  Multiplexer multiplexer_27 (.in0(data_in[32]), .in1(not_27_out), .out(data_out[26]), .sel(decoder_1_out33));
  Multiplexer multiplexer_28 (.in0(data_in[33]), .in1(not_28_out), .out(data_out[27]), .sel(decoder_1_out34));
  Multiplexer multiplexer_29 (.in0(data_in[34]), .in1(not_29_out), .out(data_out[28]), .sel(decoder_1_out35));
  Multiplexer multiplexer_30 (.in0(data_in[35]), .in1(not_30_out), .out(data_out[29]), .sel(decoder_1_out36));
  Multiplexer multiplexer_31 (.in0(data_in[36]), .in1(not_31_out), .out(data_out[30]), .sel(decoder_1_out37));
  Multiplexer multiplexer_32 (.in0(data_in[37]), .in1(not_32_out), .out(data_out[31]), .sel(decoder_1_out38));
  Multiplexer multiplexer_33 (.in0(data_in[38]), .in1(not_33_out), .out(data_out[32]), .sel(decoder_1_out39));
  Multiplexer multiplexer_34 (.in0(data_in[39]), .in1(not_34_out), .out(data_out[33]), .sel(decoder_1_out40));
endmodule
