// Logisim project INTERRUPT_CONTROLLER.circ as structural Verilog: 1 circuit, main circuit interrupt
// INTERRUPT
module interrupt (
  input  CLK,
  input  RESET,
  input  [3:0] PC_Q,
  input  WAITING_IN,
  input  CAR_AT_ZERO,
  input  [33:0] AC_OUT,
  input  [33:0] AC_IN,
  output INITIALIZATION,
  output FINISHED,
  output BUSY_OUT,
  output [3:0] STORED_PC_OUT,
  output [33:0] AC_D
);

  wire Available_out, comparator_1_eq, multiplexer_1_out, not_1_out, or_1_out;
  wire [33:0] STORED_AC_q;

  not not_1 (not_1_out, BUSY_OUT);
  Comparator #(.width(4)) comparator_1 (.a(PC_Q), .b(4'b1101), .eq(comparator_1_eq));  // open: gt, lt
  and Available (Available_out, WAITING_IN, not_1_out);
  and and_1 (INITIALIZATION, Available_out, CAR_AT_ZERO);
  and and_2 (FINISHED, CAR_AT_ZERO, BUSY_OUT, comparator_1_eq);
  or or_1 (or_1_out, INITIALIZATION, FINISHED);
  Multiplexer multiplexer_1 (.in0(1'b1), .in1(1'b0), .out(multiplexer_1_out), .sel(FINISHED));
  Register #(.width(1)) BUSY (.D(multiplexer_1_out), .en(or_1_out), .Q(BUSY_OUT), .clk(CLK), .clr(RESET));
  Register #(.width(4)) STORED_PC (.D(PC_Q), .en(INITIALIZATION), .Q(STORED_PC_OUT), .clk(CLK), .clr(RESET));
  Register #(.width(34)) STORED_AC (.D(AC_OUT), .en(INITIALIZATION), .Q(STORED_AC_q), .clk(CLK), .clr(RESET));
  Multiplexer #(.width(34)) multiplexer_2 (.in0(AC_IN), .in1(STORED_AC_q), .out(AC_D), .sel(FINISHED));

  // Notes on the sheet:
  //   PC_AT_D
endmodule
